# Fritzing sketch esp8266_oled_display (saved by Fritzing 0.9.3b)
breadboards: 1

parts:
  U1 = NodeMCU V1.0
  Squix1 = OLED 0.96" 128x64 I2C SSD1306
  S1 = Pushbutton [package="[THT]"]
  S2 = Pushbutton [package="[THT]"]

nets:
  N1: U1.D1, Squix1.SCL
  N2: U1.D2, Squix1.SCA
  3V3: U1.3V3, Squix1.VCC
  GND: U1.GND, Squix1.GND, S1.Pin_3, S1.Pin_4, S2.Pin_3, S2.Pin_4
  N3: U1.SD2, S2.Pin_1, S2.Pin_2
  N4: U1.SD3, S1.Pin_1, S1.Pin_2

custom parts:
  NodeMCU V1.0: ESP8266 based NodeMCU
